# Fritzing sketch circuit (saved by Fritzing 0.9.6b)

parts:
  S1 = SWITCH-DPDT [package=os]
  A1 = Waveshare rp2040-zero tht [package=THT]
  BATT1 = 3xAAA Switchable Battery Pack w/JST connector
  NeoPixel_Ring1 = 24 NeoPixel Ring
  R1 = Resistor [tolerance=±5% power=0.25 resistance=1000 package=THT]
  LED1 = LED - 5mm [color="White (4500K)" current=0.030 package="5 mm [THT]"]
  LED2 = LED - 5mm [color="Infrared (940nm)" current=0.030 package="5 mm [THT]"]
  Q1 = NPN-Transistor [package="TO92 [THT]"]
  R2 = Trimmer Potentiometer [maximum_resistance=10kΩ package=THT]
  S2 = Square Pushbutton
  V1 = DC Power [voltage=5]

nets:
  N1: S1.1, BATT1.POS, V1.V+
  N2: S1.2, A1.Pin_1, NeoPixel_Ring1.VDD
  N3: A1.Pin_2, BATT1.NEG, NeoPixel_Ring1.GND, LED1.cathode, Q1.E, R2.leg1, S2.leg1, V1.V-
  N4: A1.Pin_3, R1.Pin_0, LED2.anode, R2.leg2
  N5: A1.Pin_7, R2.wiper
  N6: A1.Pin_21, S2.leg0
  N7: A1.Pin_22, Q1.B
  N8: A1.Pin_23, NeoPixel_Ring1.IN
  N9: R1.Pin_1, LED1.anode
  N10: LED2.cathode, Q1.C

custom parts:
  Waveshare rp2040-zero tht: .RP2040-Zero, A Low-Cost, High-Performance Pico-Like MCU Board Based On Raspberry Pi Microcontroller RP2040. This varant is THT without the extra connections.
  3xAAA Switchable Battery Pack w/JST connector: 3xAAA Switchable Battery Pack with JST connector
  24 NeoPixel Ring: 24 ultra bright smart LED NeoPixels are arranged in a circle with 2.6" (66mm) outer diameter. The rings are 'chainable' - connect the output pin of one to the input pin of another. Use only one microcontroller pin to control as many as you can chain together! Each LED is addressable as the driver chip is inside the LED. Each one has ~18mA constant current drive so the color will be very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
